# Fritzing sketch fritzing_htu21d (saved by Fritzing 0.9.2b)
circuit board: 8.46667cm x 5.64444cm
breadboards: 1

parts:
  Part1 = Arduino Nano (Rev3.0)
  Part2 = HTU21D Breakout
  S1 = Momentary Switch [package=ksa_sealed_tac_switch]

nets:
  GND: Part1.GND, Part2.GND, S1.3
  N1: Part1.D2, S1.1
  N2: Part1.A5, Part2.SCL
  N3: Part1.A4, Part2.SDA
  3V3: Part1.3V3, Part2.3.3V

custom parts:
  HTU21D Breakout: This is a breadboard friendly breakout board for the Measurement Specialties high-precision, low-power digital humidity sensor.
